# Fritzing sketch Coeur schéma (saved by Fritzing 0.9.3b)
breadboards: 1

parts:
  Composant1 = Arduino Uno (Rev3)
  LED2 = LED - 5mm [color="Red (633nm)" package="5 mm [THT]"]
  LED3 = LED - 5mm [color="Red (633nm)" package="5 mm [THT]"]
  LED4 = LED - 5mm [color="Red (633nm)" package="5 mm [THT]"]
  R1 = Resistor [tolerance=±5% resistance=220 package=THT]
  R2 = Resistor [tolerance=±5% resistance=220 package=THT]
  LED5 = LED - 5mm [color="Red (633nm)" package="5 mm [THT]"]
  LED6 = LED - 5mm [color="Red (633nm)" package="5 mm [THT]"]
  R3 = Resistor [tolerance=±5% resistance=220 package=THT]
  R4 = Resistor [tolerance=±5% resistance=220 package=THT]
  R5 = Resistor [tolerance=±5% resistance=220 package=THT]
  LED7 = LED - 5mm [color="Red (633nm)" package="5 mm [THT]"]
  R6 = Resistor [tolerance=±5% resistance=220 package=THT]
  LED8 = LED - 5mm [color="Red (633nm)" package="5 mm [THT]"]
  R7 = Resistor [tolerance=±5% resistance=220 package=THT]
  LED9 = LED - 5mm [color="Red (633nm)" package="5 mm [THT]"]
  R8 = Resistor [tolerance=±5% resistance=220 package=THT]
  LED10 = LED - 5mm [color="Red (633nm)" package="5 mm [THT]"]
  R9 = Resistor [tolerance=±5% resistance=220 package=THT]

nets:
  N1: Composant1.D8, Composant1.D11_PWM/MOSI, LED2.anode, LED3.anode, LED4.anode, LED5.anode, LED6.anode, LED7.anode, R6.Pin_0, LED8.cathode, LED8.anode, LED9.cathode, LED9.anode, R8.Pin_0, LED10.anode, R9.Pin_0, R9.Pin_1
  N2: Composant1.D9_PWM, R6.Pin_1
  N3: Composant1.D10_PWM/SS, R5.Pin_0, LED7.cathode
  N4: Composant1.D2, R1.Pin_0
  N5: Composant1.D3_PWM, R2.Pin_0
  N6: Composant1.D4, R3.Pin_1
  N7: Composant1.D5_PWM, R4.Pin_1
  N8: Composant1.D6_PWM, R7.Pin_1
  N9: Composant1.D7, R8.Pin_1, LED10.cathode
  N10: LED2.cathode, R1.Pin_1
  N11: LED3.cathode, R5.Pin_1
  N12: LED4.cathode, R2.Pin_1
  N13: LED5.cathode, R3.Pin_0
  N14: LED6.cathode, R4.Pin_0
