# Fritzing sketch Montage final (saved by Fritzing 0.9.3b)
breadboards: 1

parts:
  Q1 = LTR-301 [package=ltr-301]
  LED1 = LED - 5mm [color="Red (633nm)" package="5 mm [THT]"]
  R1 = Resistor [tolerance=±5% resistance=10k package=THT]
  C2 = Ceramic Capacitor [capacitance=100nF package="100 mil [THT, multilayer]"]
  Q2 = NPN-Transistor [package="TO92 [THT]"]
  R2 = Resistor [tolerance=±5% resistance=150 package=THT]
  R3 = Resistor [tolerance=±5% resistance=68k package=THT]
  R4 = Resistor [tolerance=±5% resistance=1k package=THT]
  Composant1 = Arduino Uno (Rev3)
  U1 = LM124-324 Quad Opamp [package="DIP (Dual Inline)"]
  C4 = Ceramic Capacitor [capacitance=100nF package="100 mil [THT, multilayer]"]
  R5 = Resistor [tolerance=±5% resistance=1.8k package=THT]
  R6 = Resistor [tolerance=±5% resistance=8.2k package=THT]
  R7 = Resistor [tolerance=±5% resistance=470k package=THT]
  R8 = Resistor [tolerance=±5% resistance=68k package=THT]
  C6 = Ceramic Capacitor [capacitance=100nF package="100 mil [THT, multilayer]"]
  C3 = Ceramic Capacitor [capacitance=1µF package="100 mil [THT, multilayer]"]
  R9 = Resistor [tolerance=±5% resistance=220 package=THT]

nets:
  N1: Q1.C, LED1.anode, R2.Pin_1, R3.Pin_1, Composant1.GND, U1.VCC-, R6.Pin_1, R8.Pin_1, R9.Pin_1
  N2: Q1.E, R1.Pin_1, C3.0
  N3: LED1.cathode, R4.Pin_0
  N4: R1.Pin_0, R4.Pin_1, Composant1.5V, U1.VCC+
  N5: C2.0, U1.1IN-, R6.Pin_0
  N6: C2.1, U1.1OUT, C6.0
  N7: Q2.E, R9.Pin_0
  N8: Q2.B, R5.Pin_0
  N9: Q2.C, Composant1.A0
  N10: R2.Pin_0, U1.4IN-, C4.0, R7.Pin_0
  N11: R3.Pin_0, U1.4IN+, C6.1
  N12: U1.1IN+, R8.Pin_0, C3.1
  N13: U1.4OUT, C4.1, R5.Pin_1, R7.Pin_1
